# Fritzing sketch AnalogInputDemo-Schematics (saved by Fritzing 0.9.10b)
breadboards: 1

parts:
  R1 = Rotary Potentiometer (Small) [maximum_resistance=10kΩ knob_status=50% power=0.5W package=THT]
  R8 = Resistor [tolerance=±1% resistance=1k package="1206 [SMD]"]
  R9 = Temperature Sensor (Thermistor) [thermistor_type=NTC package=THT]
  R10 = Resistor [tolerance=±1% resistance=10k package="1206 [SMD]"]
  R11 = PHOTOCELL [package=photocell-kit]
  R12 = Rotary Potentiometer (Small) [maximum_resistance=10kΩ knob_status=50% power=0.5W package=THT]
  LED1 = LED - 5mm [color="Red (633nm)" current=0.030 package="5 mm [THT]"]
  R13 = Resistor [tolerance=±1% resistance=220 package="1206 [SMD]"]

nets:
  GND: R1.leg1, R9.pin_0, R10.Pin_1, R12.leg1, R13.Pin_1
  A0 (input): R1.wiper, R8.Pin_1, R9.pin_1, R10.Pin_0, R11.P$2, R12.wiper
  5V: R1.leg2, R8.Pin_0, R11.P$1, R12.leg2
  N1: LED1.cathode, R13.Pin_0
  D10 (output): LED1.anode

notes:
  Thermistor Setup
  Potentiometer Setup
  Light-Dependent Resistor Setup
  Potentiometer-Blink-LED Setup
  Variable Resistors
