# Fritzing sketch AnalogOutputDemo-Schematics (saved by Fritzing 0.9.10b)
breadboards: 1

parts:
  R12 = Rotary Potentiometer (Small) [maximum_resistance=10kΩ knob_status=50% power=0.5W package=THT]
  LED1 = LED - 5mm [color="Red (633nm)" current=0.030 package="5 mm [THT]"]
  R13 = Resistor [tolerance=±1% resistance=220 package="1206 [SMD]"]
  R16 = Resistor [tolerance=±5% resistance=10k power=0.25 package=THT]
  S2 = Pushbutton [package=THT]
  R17 = Resistor [tolerance=±1% resistance=220 package="1206 [SMD]"]
  LED4 = LED - 5mm [color="Red (633nm)" current=0.030 package="5 mm [THT]"]
  R18 = Resistor [tolerance=±1% resistance=220 package="1206 [SMD]"]
  R19 = Resistor [tolerance=±1% resistance=220 package="1206 [SMD]"]
  LED5 = LED - 5mm [color="Red (633nm)" current=0.030 package="5 mm [THT]"]
  LED6 = LED - 5mm [color="Red (633nm)" current=0.030 package="5 mm [THT]"]
  R20 = Resistor [tolerance=±1% resistance=220 package="1206 [SMD]"]
  LED7 = LED - 5mm [color="Red (633nm)" current=0.030 package="5 mm [THT]"]
  R15 = Resistor [tolerance=±1% resistance=220 package="1206 [SMD]"]
  LED3 = LED - 5mm [color="Red (633nm)" current=0.030 package="5 mm [THT]"]
  LED2 = LED - 5mm [color="Red (633nm)" current=0.030 package="5 mm [THT]"]
  R1 = Rotary Potentiometer (Small) [maximum_resistance=10kΩ knob_status=50% power=0.5W package=THT]
  R14 = Resistor [tolerance=±1% resistance=220 package="1206 [SMD]"]
  SG1 = Buzzer 12mm [package=buzzer-ccv-kit]
  R21 = Resistor [tolerance=±5% resistance=10k power=0.25 package=THT]

nets:
  GND: R12.leg1, R13.Pin_1, R16.Pin_1, R17.Pin_1, R18.Pin_1, R19.Pin_1, R20.Pin_1, R15.Pin_1, R1.leg1, R21.Pin_1
  A0 (input): R12.wiper, R1.wiper
  5V: R12.leg2, S2.leg1, R1.leg2
  N1: LED1.cathode, R13.Pin_0
  D3 (PWM): LED1.anode, LED3.anode, LED2.anode, SG1.1
  D2 (INPUT): R16.Pin_0, S2.leg0
  N2: R17.Pin_0, LED4.cathode
  D5 (PWM): LED4.anode
  N3: R18.Pin_0, LED5.cathode
  N4: R19.Pin_0, LED6.cathode
  D6 (PWM): LED5.anode
  D9 (PWM): LED6.anode
  N5: R20.Pin_0, LED7.cathode
  D10 (PWM): LED7.anode
  N6: R15.Pin_0, LED3.cathode
  N7: LED2.cathode, R14.Pin_0
  N8: SG1.2, R21.Pin_0

notes:
  Brightness Control - Multiple LEDs with Pot and Switch
  Brightness Fade with Potentiometer
  Basic Brightness Fade
  Analog Output
  Passive Piezo Buzzer
