# Fritzing sketch InputPullResistors (saved by Fritzing 1.0.6)
breadboards: 1

parts:
  R1 = Resistor [tolerance=±5% resistance=10k package="0805 [SMD]"]
  Part1 = Arduino Uno (Rev3) - ICSP
  R2 = Resistor [tolerance=±5% resistance=10k package="0805 [SMD]"]
  S2 = Momentary Switch [package=ksa_sealed_tac_switch]
  S3 = Momentary Switch [package=ksa_sealed_tac_switch]
  S4 = Momentary Switch [package=ksa_sealed_tac_switch]

nets:
  GND: R1.Pin_0, Part1.GND, S2.1, S4.1
  D12: R1.Pin_1, Part1.D12/MISO, R2.Pin_0, S2.3, S3.1, S4.3
  D13: Part1.D13/SCK
  5V: Part1.5V, R2.Pin_1, S3.3

notes:
  Pull Up Resistor
  Pull Down Resistor
  INPUT Pull Up Resistor
  You Must Use "INPUT_PULLUP" in pinMode(...), or you will fry your Arduino!
