# Fritzing sketch digital-logic-demo-schematics (saved by Fritzing 1.0.6)
breadboards: 1

parts:
  HC-SR04_Sensor_1 = HC-SR04 Ultrasonic Distance Sensor
  IR1 = TSOP312.., 314.. [package=THT]

nets:
  5V: HC-SR04_Sensor_1.VCC, IR1.Vs
  D4: HC-SR04_Sensor_1.TRIG
  D3: HC-SR04_Sensor_1.ECHO
  GND: HC-SR04_Sensor_1.GND, IR1.GND
  D2: IR1.Data

notes:
  HC-SR04 Ultrasonic Distance Sensor
  IR Receiver
