# Fritzing sketch MotorDemos-Schematics (saved by Fritzing 0.9.10b)
breadboards: 1

parts:
  DC_Motor_5V = DC Motor [voltage_(max)=6V voltage_(min)=3V]
  2N222A_NPN_Transistor = NPN-Transistor [package="TO92 [THT]"]
  SM2 = 28BYJ-48 Stepper Motor [part_number=28BYJ-48]
  Driver2 = 28BYJ-48 Driver Module [part_number=ULN2003 package=THT]
  Flyback/Snubber_Diode = Rectifier Diode [part_number=1N4007 package="300 mil [THT]"]
  R1 = Resistor [tolerance=±5% resistance=220 package="0402 [SMD]"]
  J1 = Basic Servo
  DC_Motor_5V1 = DC Motor [voltage_(max)=6V voltage_(min)=3V]
  DC_Motor_5V2 = DC Motor [voltage_(max)=6V voltage_(min)=3V]
  Flyback/Snubber_Diode_1 = Rectifier Diode [part_number=1N4007 package="300 mil [THT]"]

nets:
  5V: DC_Motor_5V.pin_1, Driver2.Vmotor, Flyback/Snubber_Diode.cathode, J1.vcc, DC_Motor_5V1.pin_1, DC_Motor_5V2.pin_1, Flyback/Snubber_Diode_1.cathode
  N1: DC_Motor_5V.pin_2, 2N222A_NPN_Transistor.C, Flyback/Snubber_Diode.anode
  GND: 2N222A_NPN_Transistor.E, Driver2.GND, J1.gnd, DC_Motor_5V1.pin_2, DC_Motor_5V2.pin_2, Flyback/Snubber_Diode_1.anode
  N2: 2N222A_NPN_Transistor.B, R1.Pin_1
  N3: SM2.blue-pin, Driver2.blue-pin
  N4: SM2.pink-pin, Driver2.pink-pin
  N5: SM2.yellow-pin, Driver2.yellow-pin
  N6: SM2.orange-pin, Driver2.orange-pin
  N7: SM2.red-pin, Driver2.red-pin
  D11: Driver2.IN1
  D10: Driver2.IN2
  D9: Driver2.IN3
  D8: Driver2.IN4
  D6 (PWM): R1.Pin_0
  D3 (PWM): J1.pulse

notes:
  Motors
  DC Motor with NPN Transistor
  Power Supply Module
  Stepper Motor w/ UNL2003 Driver
  USE THE POWER SUPPLY +5V
  FOR MOTOR +5V CONNECTION
  (not the arduino 5v -- this could fry your arduino!)
  Arduino Ground
  Power Supply Ground
  Common Ground
  We need to link the grounds of the Arduino and Power Supply to have a common ground (reference voltage), otherwise nothing will work properly!
  Servo Motor
  DC Motor (No Control)
  DC Motor with Flyback Diode

custom parts:
  28BYJ-48 Stepper Motor: Unipolar Stepper Motor 28BYJ-48 Top coil - pink & orange Bottom coil - blue & yellow Common rail - red Connector pins: blue - pink - yellow - orange - red
  28BYJ-48 Driver Module: Generic male header
